# Fritzing sketch Robotoplatform (saved by Fritzing 0.9.2b)
breadboards: 1

parts:
  Raspberry_Pi1 = Raspberry Pi 2
  Part1 = Arduino Uno (Rev3)
  J1 = Basic Servo

nets:
  N1: Raspberry_Pi1.GPIO2, Part1.A4/SDA
  N2: Raspberry_Pi1.GPIO3, Part1.A5/SCL
  GND: Raspberry_Pi1.GND, Part1.GND, J1.gnd
  N3: Part1.D8, J1.pulse
  3V3: Part1.3V3, J1.vcc
